# Fritzing sketch DHT11_calibration_schematic (saved by Fritzing 0.9.3b)
breadboards: 1

parts:
  Part1 = Arduino Uno (Rev3)
  RHT1 = Humidity and Temperature Sensor RHT03

nets:
  N1: Part1.D8, RHT1.Data-signal
  5V: Part1.5V, RHT1.Vcc
  N2: Part1.GND, RHT1.GND_2
