# Fritzing sketch ds3231_calibration_schematic (saved by Fritzing 0.9.3b)
breadboards: 1

parts:
  ZS-042_RTC1 = ZS-042 RTC Module
  Part1 = Arduino Uno (Rev3)

nets:
  GND: ZS-042_RTC1.GND, Part1.GND
  VCC: ZS-042_RTC1.VCC, Part1.5V
  N1: ZS-042_RTC1.SDA, Part1.A5/SCL
  N2: ZS-042_RTC1.SCL, Part1.A4/SDA
