# Fritzing sketch soil_moisture_sensor_calibration_schematic (saved by Fritzing 0.9.3b)

parts:
  부품1 = FC-28 Soil Hygrometer Module - Probe
  부품2 = FC-28 Soil Hygrometer Module
  부품3 = Arduino Uno (Rev3)

nets:
  N1: 부품1.POS, 부품2.POS
  N2: 부품1.NEG, 부품2.NEG
  VCC: 부품2.VCC, 부품3.5V
  GND: 부품2.GND, 부품3.GND
  N3: 부품2.AO, 부품3.A1

custom parts:
  FC-28 Soil Hygrometer Module - Probe: The FC-28 is a soil hygrometer module that uses the Texas Instruments LM393 comparator chip to provide an analog measurement of soil humidity.
  FC-28 Soil Hygrometer Module: The FC-28 is a soil hygrometer module that uses the Texas Instruments LM393 comparator chip to provide an analog measurement of soil humidity. The digital output is high when soil moisture is over a certain threshold, as determined by adjusting the potentiometer.
