# Fritzing sketch final_monitoring_system_schematic (saved by Fritzing 0.9.3b)
breadboards: 2

parts:
  Part1 = Arduino Uno (Rev3)
  ZS-042_RTC1 = ZS-042 RTC Module
  부품3 = FC-28 Soil Hygrometer Module - Probe
  부품4 = FC-28 Soil Hygrometer Module
  RHT1 = Humidity and Temperature Sensor RHT03
  R1 = PHOTOCELL [package=photocell]
  Part2 = MicroSD Card Module
  R2 = Resistor [tolerance=±5% resistance=220 package="0603 [SMD]"]
  LED1 = smd LED [color="Red (633nm)" package="1206 [SMD]"]

nets:
  N1: Part1.A0, R1.P$2, R2.Pin_0
  N2: Part1.A1, 부품4.AO
  N3: Part1.D8, RHT1.Data-signal
  N4: Part1.D10_PWM/SS, Part2.CS
  N5: Part1.D11_PWM/MOSI, Part2.MISO
  N6: Part1.D12/MISO, Part2.MOSI
  N7: Part1.D13/SCK, Part2.SCK
  GND: Part1.GND, ZS-042_RTC1.GND, 부품4.GND, RHT1.GND_2, Part2.GND, R2.Pin_1, LED1.cathode
  VCC: Part1.D2, 부품4.VCC, RHT1.Vcc, R1.P$1
  N8: Part1.D4, LED1.anode
  VCC_2: Part1.5V, ZS-042_RTC1.VCC, Part2.VCC
  N9: 부품3.POS, 부품4.POS
  N10: 부품3.NEG, 부품4.NEG

custom parts:
  FC-28 Soil Hygrometer Module - Probe: The FC-28 is a soil hygrometer module that uses the Texas Instruments LM393 comparator chip to provide an analog measurement of soil humidity.
  FC-28 Soil Hygrometer Module: The FC-28 is a soil hygrometer module that uses the Texas Instruments LM393 comparator chip to provide an analog measurement of soil humidity. The digital output is high when soil moisture is over a certain threshold, as determined by adjusting the potentiometer.
